# Fritzing sketch micro (saved by Fritzing 0.9.3b)
breadboards: 1

parts:
  Composant1 = Arduino Micro (Rev3)  # not connected
  S1 = Pushbutton [package="[THT]"]
  LED1 = LED - 5mm [color="Red (633nm)" package="5 mm [THT]"]
  R1 = Resistor [tolerance=±5% resistance=220 package=THT]
  R2 = Trimmer Potentiometer [maximum_resistance=10kΩ package=THT]

nets:
  N1: S1.Pin_1, S1.Pin_2, R1.Pin_0, R2.leg1
  N2: S1.Pin_3, S1.Pin_4
  N3: LED1.cathode, R1.Pin_1
